// Logisim project smart water tank circ.circ as structural Verilog: 1 circuit, main circuit main
module main (
  input  in_1,
  input  in_2,
  input  in_3,
  output out_4,
  output out_5
);

  wire and_2_out, and_3_out, not_1_out, not_2_out, not_3_out, or_1_out, undriven, undriven_2;

  not not_1 (not_1_out, in_2);
  not not_2 (not_2_out, in_3);
  not not_3 (not_3_out, in_1);
  or or_1 (or_1_out, in_1, not_1_out);
  and and_1 (out_4, or_1_out, not_2_out);
  and and_2 (and_2_out, not_3_out, in_2);
  and and_3 (and_3_out, not_1_out, in_3);
  or or_2 (out_5, and_2_out, and_3_out);
  LED led_1 (.in(undriven));
  LED led_2 (.in(undriven_2));
endmodule
